// Digital circuit 74138-RD.dig as structural Verilog
// 3-line to 8-line decoder/demultiplexer, inverted out
module _74138_RD (
  input  A0,
  input  A1,
  input  A2,
  input  nGA,
  input  nGB,
  input  G,
  input  VCC,
  input  GND,
  output nY0,
  output nY1,
  output nY2,
  output nY3,
  output nY4,
  output nY5,
  output nY6,
  output nY7
);

  wire nand_1_out;
  wire [2:0] delay_1_out;

  PowerSupply powersupply_1 (.VDD(VCC), .GND(GND));
  nand nand_1 (nand_1_out, G, ~nGB, ~nGA);  // NAnd
  Delay #(.Bits(3)) delay_1 (.in({A2, A1, A0}), .out(delay_1_out));
  Demultiplexer #(.Selector_Bits(3), .Default(1)) demultiplexer_1 (
    .sel(delay_1_out), .in(nand_1_out), .out_0(nY0), .out_1(nY1), .out_2(nY2), .out_3(nY3), .out_4(nY4),
    .out_5(nY5), .out_6(nY6), .out_7(nY7));

  // Notes on the sheet:
  //   A0: pin 1
  //   A1: pin 2
  //   A2: pin 3
  //   nGA: pin 4
  //   nGB: pin 5
  //   G: pin 6
  //   nY0: pin 15
  //   nY1: pin 14
  //   nY2: pin 13
  //   nY3: pin 12
  //   nY4: pin 11
  //   nY5: pin 10
  //   nY6: pin 9
  //   nY7: pin 7
  //   VCC: pin 16, default 1
  //   GND: pin 8
endmodule

/* Test case:
~GA ~GB G A B C ~Y0 ~Y1 ~Y2 ~Y3 ~Y4 ~Y5 ~Y6 ~Y7

 1   X  X X X X  1   1   1   1   1   1   1   1
 X   1  X X X X  1   1   1   1   1   1   1   1
 X   X  0 X X X  1   1   1   1   1   1   1   1

 0   0  1 0 0 0  0   1   1   1   1   1   1   1
 0   0  1 1 0 0  1   0   1   1   1   1   1   1
 0   0  1 0 1 0  1   1   0   1   1   1   1   1
 0   0  1 1 1 0  1   1   1   0   1   1   1   1
 0   0  1 0 0 1  1   1   1   1   0   1   1   1
 0   0  1 1 0 1  1   1   1   1   1   0   1   1
 0   0  1 0 1 1  1   1   1   1   1   1   0   1
 0   0  1 1 1 1  1   1   1   1   1   1   1   0
*/
