// Digital circuit 74161-RD.dig as structural Verilog
// hex synchronous counter, async clear
module _74161_RD (
  input  nSPE,
  input  nMR,
  input  CP,
  input  TE,
  input  PE,
  input  A,
  input  B,
  input  C,
  input  D,
  input  VCC,
  input  GND,
  output TC,
  output Q0,
  output Q1,
  output Q2,
  output Q3
);

  wire add_1_c_o, and_1_out;
  wire [3:0] add_1_s, multiplexer_1_out, multiplexer_2_out;

  PowerSupply powersupply_1 (.VDD(VCC), .GND(GND));
  Add #(.Bits(4)) add_1 (.a({Q3, Q2, Q1, Q0}), .b(4'b0001), .c_i(1'b0), .s(add_1_s), .c_o(add_1_c_o));
  and and_1 (and_1_out, PE, TE);
  Multiplexer #(.Bits(4)) multiplexer_1 (
    .sel(and_1_out), .in_0({Q3, Q2, Q1, Q0}), .in_1(add_1_s), .out(multiplexer_1_out));
  Multiplexer #(.Bits(4)) multiplexer_2 (
    .sel(nSPE), .in_0({D, C, B, A}), .in_1(multiplexer_1_out), .out(multiplexer_2_out));
  and and_2 (TC, add_1_c_o, TE);
  D_FF_AS #(.Bits(4)) d_ff_as_1 (
    .Set(1'b0), .D(multiplexer_2_out), .C(CP), .Clr(~nMR), .Q({Q3, Q2, Q1, Q0}));  // open: nQ

  // Notes on the sheet:
  //   nSPE: pin 9
  //   nMR: pin 1
  //   CP: pin 2
  //   TC: pin 15
  //   TE: pin 10
  //   PE: pin 7
  //   A: pin 3
  //   B: pin 4
  //   C: pin 5
  //   D: pin 6
  //   Q0: pin 14
  //   Q1: pin 13
  //   Q2: pin 12
  //   Q3: pin 11
  //   VCC: pin 16, default 1
  //   GND: pin 8
endmodule
