// Digital circuit 7420-RD.dig as structural Verilog
// dual 4-input NAND gate
module _7420_RD (
  input  _1A,
  input  _1C,
  input  _2A,
  input  _2C,
  input  _1B,
  input  _2B,
  input  _1D,
  input  _2D,
  input  VCC,
  input  GND,
  output _1Y,
  output _2Y
);

  PowerSupply powersupply_1 (.VDD(VCC), .GND(GND));
  nand nand_1 (_1Y, _1A, _1B, _1C, _1D);
  nand nand_2 (_2Y, _2A, _2B, _2C, _2D);

  // Notes on the sheet:
  //   _1A: pin 1
  //   _1C: pin 4
  //   _1Y: pin 6
  //   _2A: pin 9
  //   _2C: pin 12
  //   _2Y: pin 8
  //   _1B: pin 2
  //   _2B: pin 10
  //   _1D: pin 5
  //   _2D: pin 13
  //   VCC: pin 14, default 1
  //   GND: pin 7
endmodule
