// Digital circuit 74245-RD.dig as structural Verilog
// octal bus transceivers with 3-state outputs
module _74245_RD (
  input  DIR,
  input  nOE,
  input  A1,
  input  B1,
  input  A2,
  input  B2,
  input  A3,
  input  B3,
  input  A4,
  input  B4,
  input  A5,
  input  B5,
  input  A6,
  input  B6,
  input  A7,
  input  B7,
  input  A8,
  input  B8,
  input  VCC,
  input  GND
);

  wire and_1_out, and_2_out;

  PowerSupply powersupply_1 (.VDD(VCC), .GND(GND));
  and and_1 (and_1_out, DIR, ~nOE);  // And
  assign B1 = and_1_out ? A1 : 1'bz;  // Driver driver_1
  assign B2 = and_1_out ? A2 : 1'bz;  // Driver driver_2
  assign B3 = and_1_out ? A3 : 1'bz;  // Driver driver_3
  assign B4 = and_1_out ? A4 : 1'bz;  // Driver driver_4
  assign B5 = and_1_out ? A5 : 1'bz;  // Driver driver_5
  assign B6 = and_1_out ? A6 : 1'bz;  // Driver driver_6
  assign B7 = and_1_out ? A7 : 1'bz;  // Driver driver_7
  assign B8 = and_1_out ? A8 : 1'bz;  // Driver driver_8
  assign A1 = and_2_out ? B1 : 1'bz;  // Driver driver_9
  assign A2 = and_2_out ? B2 : 1'bz;  // Driver driver_10
  assign A3 = and_2_out ? B3 : 1'bz;  // Driver driver_11
  assign A4 = and_2_out ? B4 : 1'bz;  // Driver driver_12
  assign A5 = and_2_out ? B5 : 1'bz;  // Driver driver_13
  assign A6 = and_2_out ? B6 : 1'bz;  // Driver driver_14
  assign A7 = and_2_out ? B7 : 1'bz;  // Driver driver_15
  assign A8 = and_2_out ? B8 : 1'bz;  // Driver driver_16
  and and_2 (and_2_out, ~nOE, ~DIR);  // And

  // Notes on the sheet:
  //   DIR: pin 1
  //   nOE: pin 19
  //   A1: pin 2
  //   B1: pin 18
  //   A2: pin 3
  //   B2: pin 17
  //   A3: pin 4
  //   B3: pin 16
  //   A4: pin 5
  //   B4: pin 15
  //   A5: pin 6
  //   B5: pin 14
  //   A6: pin 7
  //   B6: pin 13
  //   A7: pin 8
  //   B7: pin 12
  //   A8: pin 9
  //   B8: pin 11
  //   VCC: pin 20, default 1
  //   GND: pin 10
endmodule
