// Digital circuit 74257-RD.dig as structural Verilog
// quad 2-line to 1-line data selectors/multiplexers (3-state output)
module _74257_RD (
  input  S,
  input  A1,
  input  A2,
  input  A3,
  input  A4,
  input  B1,
  input  B2,
  input  B3,
  input  B4,
  input  nOE,
  input  VCC,
  input  GND,
  output Y1,
  output Y2,
  output Y3,
  output Y4
);

  wire [3:0] multiplexer_1_out;

  PowerSupply powersupply_1 (.VDD(VCC), .GND(GND));
  Multiplexer #(.Bits(4)) multiplexer_1 (
    .sel(S), .in_0({A4, A3, A2, A1}), .in_1({B4, B3, B2, B1}), .out(multiplexer_1_out));
  assign {Y4, Y3, Y2, Y1} = ~nOE ? multiplexer_1_out : 4'bz;  // DriverInvSel driverinvsel_1

  // Notes on the sheet:
  //   S: select, pin 1
  //   A1: pin 2
  //   A2: pin 5
  //   A3: pin 11
  //   A4: pin 14
  //   B1: pin 3
  //   B2: pin 6
  //   B3: pin 10
  //   B4: pin 13
  //   nOE: strobe, pin 15, default 1
  //   Y1: pin 4
  //   Y2: pin 7
  //   Y3: pin 9
  //   Y4: pin 12
  //   VCC: pin 16, default 1
  //   GND: pin 8
endmodule

/* Test case:
~G S   A4 A3 A2 A1 B4 B3 B2 B1 Y4 Y3 Y2 Y1 VCC GND
 1 x   x  x  x  x  x  x  x  x  Z  Z  Z  Z  1   0 

 0 0   0  0  0  1  0  0  0  0  0  0  0  1   1   0 
 0 0   0  0  0  1  1  1  1  1  0  0  0  1   1   0 
 0 0   0  0  1  0  0  0  0  0  0  0  1  0   1   0 
 0 0   0  0  1  0  1  1  1  1  0  0  1  0   1   0 
 0 0   0  1  0  0  0  0  0  0  0  1  0  0   1   0 
 0 0   0  1  0  0  1  1  1  1  0  1  0  0   1   0 
 0 0   1  0  0  0  0  0  0  0  1  0  0  0   1   0 
 0 0   1  0  0  0  1  1  1  1  1  0  0  0   1   0 

 0 1   0  0  0  0  0  0  0  1  0  0  0  1   1   0 
 0 1   1  1  1  1  0  0  0  1  0  0  0  1   1   0 
 0 1   0  0  0  0  0  0  1  0  0  0  1  0   1   0 
 0 1   1  1  1  1  0  0  1  0  0  0  1  0   1   0 
 0 1   0  0  0  0  0  1  0  0  0  1  0  0   1   0 
 0 1   1  1  1  1  0  1  0  0  0  1  0  0   1   0 
 0 1   0  0  0  0  1  0  0  0  1  0  0  0   1   0 
 0 1   1  1  1  1  1  0  0  0  1  0  0  0   1   0 
*/
