// Digital circuit 74373-RD.dig as structural Verilog
// octal transparent latches
module _74373_RD (
  input  C,
  input  nOC,
  input  D0,
  input  D1,
  input  D2,
  input  D3,
  input  D4,
  input  D5,
  input  D6,
  input  D7,
  input  VCC,
  input  GND,
  output Q0,
  output Q1,
  output Q2,
  output Q3,
  output Q4,
  output Q5,
  output Q6,
  output Q7
);

  wire _74373_d_inc_1_pin11, _74373_d_inc_1_pin13, _74373_d_inc_1_pin15, _74373_d_inc_1_pin17,
       _74373_d_inc_2_pin11, _74373_d_inc_3_pin11, _74373_d_inc_4_pin11, _74373_d_inc_5_pin9,
       _74373_d_inc_5_pin10, _74373_d_inc_5_pin11, _74373_d_inc_5_pin12, _74373_d_inc_7_p1,
       _74373_d_inc_7_p2, _74373_d_inc_7_p3, _74373_d_inc_7_p4, _74373_d_inc_7_p5, _74373_d_inc_8_p1,
       undriven, undriven_2;

  PowerSupply powersupply_1 (.VDD(VCC), .GND(GND));
  _74373_D_inc _74373_d_inc_1 (
    .pin1(D0), .pin2(C), .pin3(D1), .pin4(C), .pin5(D2), .pin6(C), .pin7(D3), .pin8(C), .pin9(D4), .pin10(C),
    .pin11(_74373_d_inc_1_pin11), .pin12(nOC), .pin13(_74373_d_inc_1_pin13), .pin14(nOC),
    .pin15(_74373_d_inc_1_pin15), .pin16(nOC), .pin17(_74373_d_inc_1_pin17), .pin18(nOC), .pin20(nOC));  // open: pin19
  _74373_D_inc _74373_d_inc_2 (
    .pin1(D1), .pin2(C), .pin3(D2), .pin4(C), .pin5(D3), .pin6(C), .pin7(D4), .pin8(C), .pin9(D5), .pin10(C),
    .pin11(_74373_d_inc_2_pin11), .pin12(nOC), .pin13(_74373_d_inc_1_pin11), .pin14(nOC),
    .pin15(_74373_d_inc_1_pin13), .pin16(nOC), .pin17(_74373_d_inc_1_pin15), .pin18(nOC),
    .pin19(_74373_d_inc_1_pin17), .pin20(nOC));
  _74373_D_inc _74373_d_inc_3 (
    .pin1(D2), .pin2(C), .pin3(D3), .pin4(C), .pin5(D4), .pin6(C), .pin7(D5), .pin8(C), .pin9(D6), .pin10(C),
    .pin11(_74373_d_inc_3_pin11), .pin12(nOC), .pin13(_74373_d_inc_2_pin11), .pin14(nOC),
    .pin15(_74373_d_inc_1_pin11), .pin16(nOC), .pin17(_74373_d_inc_1_pin13), .pin18(nOC),
    .pin19(_74373_d_inc_1_pin15), .pin20(nOC));
  _74373_D_inc _74373_d_inc_4 (
    .pin1(D3), .pin2(C), .pin3(D4), .pin4(C), .pin5(D5), .pin6(C), .pin7(D6), .pin8(C), .pin9(D7), .pin10(C),
    .pin11(_74373_d_inc_4_pin11), .pin12(nOC), .pin13(_74373_d_inc_3_pin11), .pin14(nOC),
    .pin15(_74373_d_inc_2_pin11), .pin16(nOC), .pin17(_74373_d_inc_1_pin11), .pin18(nOC),
    .pin19(_74373_d_inc_1_pin13), .pin20(nOC));
  _74373_D_inc _74373_d_inc_5 (
    .pin1(D4), .pin2(C), .pin3(D5), .pin4(C), .pin5(D6), .pin6(C), .pin7(D7), .pin8(C),
    .pin9(_74373_d_inc_5_pin9), .pin10(_74373_d_inc_5_pin10), .pin11(_74373_d_inc_5_pin11),
    .pin12(_74373_d_inc_5_pin12), .pin13(_74373_d_inc_4_pin11), .pin14(nOC), .pin15(_74373_d_inc_3_pin11),
    .pin16(nOC), .pin17(_74373_d_inc_2_pin11), .pin18(nOC), .pin19(_74373_d_inc_1_pin11), .pin20(nOC));
  _74373_D_inc _74373_d_inc_6 (
    .pin1(D5), .pin2(C), .pin3(D6), .pin4(C), .pin5(D7), .pin6(C), .pin7(_74373_d_inc_5_pin9),
    .pin8(_74373_d_inc_5_pin10), .pin13(_74373_d_inc_5_pin11), .pin14(_74373_d_inc_5_pin12),
    .pin15(_74373_d_inc_4_pin11), .pin16(nOC), .pin17(_74373_d_inc_3_pin11), .pin18(nOC),
    .pin19(_74373_d_inc_2_pin11), .pin20(nOC));  // open: pin9, pin10, pin11, pin12
  // _74373_D_inc _74373_d_inc_7: pin names not known; wires that end beside it: _74373_d_inc_7_p1, _74373_d_inc_7_p2, _74373_d_inc_7_p3, _74373_d_inc_7_p4, _74373_d_inc_7_p5
  // _74373_D_inc _74373_d_inc_8: pin names not known; wires that end beside it: _74373_d_inc_8_p1
  assign Q0 = ~nOC ? undriven : 1'bz;  // DriverInvSel driverinvsel_1
  assign Q1 = ~nOC ? undriven_2 : 1'bz;  // DriverInvSel driverinvsel_2
  assign Q2 = ~nOC ? _74373_d_inc_7_p1 : 1'bz;  // DriverInvSel driverinvsel_3
  assign Q3 = ~nOC ? _74373_d_inc_7_p2 : 1'bz;  // DriverInvSel driverinvsel_4
  assign Q4 = ~nOC ? _74373_d_inc_7_p3 : 1'bz;  // DriverInvSel driverinvsel_5
  assign Q5 = ~nOC ? _74373_d_inc_7_p4 : 1'bz;  // DriverInvSel driverinvsel_6
  assign Q6 = ~nOC ? _74373_d_inc_7_p5 : 1'bz;  // DriverInvSel driverinvsel_7
  assign Q7 = ~nOC ? _74373_d_inc_8_p1 : 1'bz;  // DriverInvSel driverinvsel_8

  // Notes on the sheet:
  //   Q0: pin 2
  //   Q1: pin 5
  //   Q2: pin 6
  //   Q3: pin 9
  //   C: pin 11
  //   nOC: pin 1, default 1
  //   Q4: pin 12
  //   Q5: pin 15
  //   Q6: pin 16
  //   Q7: pin 19
  //   D0: pin 3
  //   D1: pin 4
  //   D2: pin 7
  //   D3: pin 8
  //   D4: pin 13
  //   D5: pin 14
  //   D6: pin 17
  //   D7: pin 18
  //   VCC: pin 20, default 1
  //   GND: pin 10
endmodule
