// Digital circuit 7474-RD.dig as structural Verilog
// dual D-flip-flop
module _7474_RD (
  input  _1nSET,
  input  _1D,
  input  _1CLK,
  input  _1nCLR,
  input  _2nSET,
  input  _2D,
  input  _2CLK,
  input  _2nCLR,
  input  VCC,
  input  GND,
  output _1Q,
  output _1nQ,
  output _2Q,
  output _2nQ
);

  wire and_1_out, and_2_out, d_ff_as_1_nq, d_ff_as_2_nq;

  PowerSupply powersupply_1 (.VDD(VCC), .GND(GND));
  D_FF_AS d_ff_as_1 (.Set(~_1nSET), .D(_1D), .C(_1CLK), .Clr(~_1nCLR), .Q(_1Q), .nQ(d_ff_as_1_nq));
  D_FF_AS d_ff_as_2 (.Set(~_2nSET), .D(_2D), .C(_2CLK), .Clr(~_2nCLR), .Q(_2Q), .nQ(d_ff_as_2_nq));
  and and_1 (and_1_out, ~_1nSET, ~_1nCLR);  // And
  and and_2 (and_2_out, ~_2nSET, ~_2nCLR);  // And
  or or_1 (_1nQ, d_ff_as_1_nq, and_1_out);
  or or_2 (_2nQ, d_ff_as_2_nq, and_2_out);

  // Notes on the sheet:
  //   _1Q: pin 5
  //   _1nQ: pin 6
  //   _1nSET: pin 4
  //   _1D: pin 2
  //   _1CLK: pin 3
  //   _1nCLR: pin 1
  //   _2Q: pin 9
  //   _2nQ: pin 8
  //   _2nSET: pin 10
  //   _2D: pin 12
  //   _2CLK: pin 11
  //   _2nCLR: pin 13
  //   VCC: pin 14, default 1
  //   GND: pin 7
endmodule

/* Test case #1:
1~SET 1~CLR 1CLK 1D 1Q 1~Q
0 1 X X 1 0
1 0 X X 0 1
0 0 X X 1 1

1 1 C 1 1 0
1 1 0 X 1 0

1 1 C 0 0 1
1 1 0 X 0 1
*/

/* Test case #2:
2~SET 2~CLR 2CLK 2D 2Q 2~Q
0 1 X X 1 0
1 0 X X 0 1
0 0 X X 1 1

1 1 C 1 1 0
1 1 0 X 1 0

1 1 C 0 0 1
1 1 0 X 0 1
*/
