// Digital circuit 8BitBuffer.dig as structural Verilog
module _8BitBuffer (
  input  [7:0] IN,
  input  nOE,
  output [7:0] OUT
);

  _74245_RD _74245_rd_1 (
    .nOE(nOE), .DIR(1'b1), .A1(IN[0]), .A2(IN[1]), .A3(IN[2]), .A4(IN[3]), .A5(IN[4]), .A6(IN[5]),
    .A7(IN[6]), .A8(IN[7]), .B1(OUT[0]), .B2(OUT[1]), .B3(OUT[2]), .B4(OUT[3]), .B5(OUT[4]), .B6(OUT[5]),
    .B7(OUT[6]), .B8(OUT[7]), .VCC(1'b1), .GND(1'b0));
endmodule
