// Digital circuit ALU.dig as structural Verilog
module ALU (
  input  [7:0] A,
  input  [7:0] B,
  input  nOE,
  input  [4:0] OP,
  input  NoBCD,
  input  nSBC,
  input  nDECIMAL,
  output [7:0] OUT,
  output nCarry8,
  output SUM_7
);

  wire C4, C8;
  wire [2:0] _74181_rd_2_nf3;
  wire [3:0] _74181_rd_1_nf3;
  wire [7:0] bcdadjustment_1_out;

  _74181_RD _74181_rd_1 (
    .Cn(1'b0), .nA3(A[0]), .nA2(A[1]), .nA1(A[2]), .nA0(A[3]), .nB3(B[0]), .nB2(B[1]), .nB1(B[2]),
    .nB0(B[3]), .S0(OP[0]), .S1(OP[1]), .S2(OP[2]), .S3(OP[3]), .M(OP[4]), .nF3(_74181_rd_1_nf3[0]),
    .nF2(_74181_rd_1_nf3[1]), .nF1(_74181_rd_1_nf3[2]), .nF0(_74181_rd_1_nf3[3]), .Cn_plus_4(C4), .VCC(1'b1),
    .GND(1'b0));  // open: nG, nP, A_eq_B
  _74181_RD _74181_rd_2 (
    .Cn(C4), .nA3(A[4]), .nA2(A[5]), .nA1(A[6]), .nA0(A[7]), .nB3(B[4]), .nB2(B[5]), .nB1(B[6]), .nB0(B[7]),
    .S0(OP[0]), .S1(OP[1]), .S2(OP[2]), .S3(OP[3]), .M(OP[4]), .nF3(_74181_rd_2_nf3[0]),
    .nF2(_74181_rd_2_nf3[1]), .nF1(_74181_rd_2_nf3[2]), .nF0(SUM_7), .Cn_plus_4(C8), .VCC(1'b1), .GND(1'b0));  // open: nG, nP, A_eq_B
  BCDAdjustment bcdadjustment_1 (
    .Sum({SUM_7, _74181_rd_2_nf3, _74181_rd_1_nf3}), .C4(C4), .ALUC8(C8), .NoBCD(NoBCD), .nDECIMAL(nDECIMAL),
    .nSBC(nSBC), .OUT(bcdadjustment_1_out));
  _74245_RD _74245_rd_1 (
    .nOE(nOE), .DIR(1'b1), .A1(bcdadjustment_1_out[0]), .A2(bcdadjustment_1_out[1]),
    .A3(bcdadjustment_1_out[2]), .A4(bcdadjustment_1_out[3]), .A5(bcdadjustment_1_out[4]),
    .A6(bcdadjustment_1_out[5]), .A7(bcdadjustment_1_out[6]), .A8(bcdadjustment_1_out[7]), .B1(OUT[0]),
    .B2(OUT[1]), .B3(OUT[2]), .B4(OUT[3]), .B5(OUT[4]), .B6(OUT[5]), .B7(OUT[6]), .B8(OUT[7]), .VCC(1'b1),
    .GND(1'b0));
  not not_1 (nCarry8, C8);

  // Other names for the same wires on the sheet: BLOW[3:0] = B[3:0]; OP_t[3:0] = OP[3:0]; M = OP[4]

  // Notes on the sheet:
  //   NoBCD: default 1
  //   nSBC: default 1
  //   nDECIMAL: default 1
endmodule
