// Digital circuit AddrDecode.dig as structural Verilog
module AddrDecode (
  input  [15:0] ADDR,
  input  nMAccess,
  output nCSRAM0,
  output nCSRAM1,
  output nCSROM,
  output nCSKB,
  output nCSTERM
);

  wire nCSIO;

  _74139_RD _74139_rd_1 (
    .n1G(nMAccess), ._1A(ADDR[14]), ._1B(ADDR[15]), .n2G(nCSIO), ._2A(ADDR[0]), ._2B(ADDR[1]),
    .n1Y0(nCSRAM0), .n1Y1(nCSRAM1), .n1Y2(nCSIO), .n1Y3(nCSROM), .n2Y0(nCSKB), .n2Y2(nCSTERM), .VCC(1'b1),
    .GND(1'b0));  // open: n2Y1, n2Y3

  // Other names for the same wires on the sheet: A_0 = ADDR[0]; ADDR14[13:0] = ADDR[13:0]; A_1 = ADDR[1]

  // Notes on the sheet:
  //   nMAccess: default 1
endmodule

/* Test case:
  ~MemAccess    ADDR  ~CSRAM0  ~CSRAM1  ~CSROM  ~CSKB  ~CSTERM
           1       x        1        1       1      1        1
# memory
           0  0x0000        0        1       1      1        1
           0  0x4000        1        0       1      1        1
           0  0xC000        1        1       0      1        1
# keyboard
           0  0x8000        1        1       1      0        1
#terminal
           0  0x8002        1        1       1      1        0
*/
