// Digital circuit BCDAdjustment.dig as structural Verilog
module BCDAdjustment (
  input  [7:0] Sum,
  input  ALUC8,
  input  C4,
  input  NoBCD,
  input  nDECIMAL,
  input  nSBC,
  output [7:0] OUT
);

  wire _74151_rd_1_y, _74151_rd_2_y, _74283_rd_1_c4, Add, and_3_out, and_4_out, and_5_out, and_6_out, nAdd,
       nor_1_out, not_1_out, or_1_out, or_2_out, Subtract;

  nor nor_1 (nor_1_out, NoBCD, nDECIMAL);
  not not_1 (not_1_out, nSBC);
  and and_1 (Add, nSBC, nor_1_out);
  and and_2 (Subtract, nor_1_out, not_1_out);
  not not_2 (nAdd, Add);
  and and_3 (and_3_out, _74283_rd_1_c4, Sum[4]);
  or or_1 (or_1_out, Sum[5], Sum[6]);
  _74151_RD _74151_rd_1 (
    .Y(_74151_rd_1_y), .nG(nAdd), .D0(1'b0), .D1(1'b0), .D2(Sum[1]), .D3(1'b1), .D4(1'b1), .D5(1'b1),
    .D6(1'b1), .D7(1'b1), .A(Sum[2]), .B(Sum[3]), .C(Sum[4]), .VCC(1'b1), .GND(1'b0));  // open: W
  _74151_RD _74151_rd_2 (
    .Y(_74151_rd_2_y), .nG(nAdd), .D0(1'b0), .D1(1'b0), .D2(and_3_out), .D3(1'b1), .D4(1'b1), .D5(1'b1),
    .D6(1'b1), .D7(1'b1), .A(or_1_out), .B(Sum[3]), .C(Sum[4]), .VCC(1'b1), .GND(1'b0));  // open: W
  and and_4 (and_4_out, ALUC8, Subtract);
  and and_5 (and_5_out, C4, Subtract);
  and and_6 (and_6_out, _74283_rd_1_c4, Add);
  or or_2 (or_2_out, _74151_rd_2_y, and_4_out);
  _74283_RD _74283_rd_1 (
    .C0(1'b0), .A1(Sum[0]), .A2(Sum[1]), .A3(Sum[2]), .A4(Sum[3]), .B1(_74151_rd_1_y), .B2(and_5_out),
    .B3(1'b0), .B4(and_5_out), .S1(OUT[0]), .S2(OUT[1]), .S3(OUT[2]), .S4(OUT[3]), .C4(_74283_rd_1_c4),
    .VCC(1'b1), .GND(1'b0));
  _74283_RD _74283_rd_2 (
    .C0(and_6_out), .A1(Sum[4]), .A2(Sum[5]), .A3(Sum[6]), .A4(Sum[7]), .B1(1'b0), .B2(or_2_out),
    .B3(_74151_rd_2_y), .B4(and_4_out), .S1(OUT[4]), .S2(OUT[5]), .S3(OUT[6]), .S4(OUT[7]), .VCC(1'b1),
    .GND(1'b0));  // open: C4

  // Other names for the same wires on the sheet: S0 = Sum[0]; S1 = Sum[1]; S2 = Sum[2]; S3 = Sum[3]; S4 = Sum[4];
  //   S5 = Sum[5]; S6 = Sum[6]; S7 = Sum[7]
endmodule
