// Digital circuit CPUTop.dig as structural Verilog
module CPUTop (
  input  CLK,
  input  RESET
);

  wire addrdecode_1_ncsram0, addrdecode_1_ncsram1, addrdecode_1_ncsrom, ALUOp, AREG_7, BREG_0, BREG_6,
       BREG_7, CarryONE, CarryZERO, Constant, IREGLoad, nACCCLK, nACCOE, nALUOE, nAREGCLK, nAREGOE, nBITOP,
       nBREGCLK, nBREGOE, nCarry, nCarry0, nCarry8, nCONSTOE, nDecimal, nEAHCLK, nEAHOE, nEALCLK, nEBHCLK,
       nEBHOE, nEBLCLK, nEBLOE, nFlagInst, nMAccess, nMWrite, NoBCD, not_1_out, not_2_out, not_3_out,
       not_4_out, not_5_out, not_6_out, not_7_out, not_8_out, not_9_out, not_10_out, not_11_out, not_12_out,
       not_13_out, not_14_out, nPCClockHigh, nPCClockLow, nPCHCLK, nPCHOE, nPCLCLK, nPCLOE, nPCSel, nSBC,
       nShiftRight, nSPREGCLK, nSPREGOE, nSTREGCLK, nSTREGOE, nUpdateC, nUpdateNZ, nUpdateV, nXREGCLK,
       nXREGOE, nYREGCLK, nYREGOE, RESET_t, SEQCNT, SUM_7;
  wire [5:1] B_out;
  wire [6:0] A_out, StatusFlags;
  wire [7:0] INSTR, memorybank_1_data;
  wire [15:0] Addr;
  wire [39:0] CtrlWord;

  // Sequencer sequencer_1: pin names not known; wires that end beside it: CLK, INSTR, {AREG_7, StatusFlags}, RESET_t, nCarry8, BREG_7, nALUOE, nAREGOE, nAREGCLK, nBREGOE, nBREGCLK, nPCHOE, nPCHCLK, nSPREGOE, nSPREGCLK, nEBHOE, nEBHCLK, nPCLOE, nPCLCLK, nACCOE, nACCCLK, nEBLOE, nEBLCLK, nSTREGOE, nSTREGCLK, nEAHOE, nEAHCLK
  PowerOnReset poweronreset_1 (.MSTRRST(RESET), .CLK(CLK), .RESET(RESET_t));  // open: nRESET
  Register EBH (.nOE(nEBHOE), .IN({AREG_7, StatusFlags}), .LD(nEBHCLK), .OUT({AREG_7, StatusFlags}));
  Register EBL (.nOE(nEBLOE), .IN({AREG_7, StatusFlags}), .LD(nEBLCLK), .OUT({AREG_7, StatusFlags}));
  Register SP (.nOE(nSPREGOE), .IN({AREG_7, StatusFlags}), .LD(nSPREGCLK), .OUT({AREG_7, StatusFlags}));
  Register Y (.nOE(nYREGOE), .IN({AREG_7, StatusFlags}), .LD(nYREGCLK), .OUT({AREG_7, StatusFlags}));
  Register X (.nOE(nXREGOE), .IN({AREG_7, StatusFlags}), .LD(nXREGCLK), .OUT({AREG_7, StatusFlags}));
  Register ACC (.nOE(nACCOE), .IN({AREG_7, StatusFlags}), .LD(nACCCLK), .OUT({AREG_7, StatusFlags}));
  // ConstRegister CONST: pin names not known; wires that end beside it: nPCSel, CarryZERO, CarryONE, nCONSTOE, Constant, nAREGCLK, {AREG_7, StatusFlags}
  Register A (.nOE(nAREGOE), .IN({AREG_7, StatusFlags}), .LD(nAREGCLK), .OUT({AREG_7, A_out}));
  Register B (.nOE(nBREGOE), .IN({AREG_7, StatusFlags}), .LD(nBREGCLK), .OUT({BREG_7, BREG_6, B_out, BREG_0}));
  INSTRegister instregister_1 (.nOE(1'b0), .IN({AREG_7, StatusFlags}), .Load(IREGLoad), .OUT(INSTR));
  not not_1 (not_1_out, nPCSel);
  Carry0 carry0_1 (.nCarry(nCarry), .CarryONE(CarryONE), .CarryZERO(CarryZERO), .nCarry0(nCarry0));
  // ALU alu_1: pin names not known; wires that end beside it: nALUOE, {AREG_7, A_out}, ALUOp, {BREG_7, BREG_6, B_out, BREG_0}, NoBCD, nSBC, nDecimal, {AREG_7, StatusFlags}, nCarry8, SUM_7
  RightShifter rightshifter_1 (
    .nShiftRight(nShiftRight), .BREG({BREG_7, BREG_6, B_out, BREG_0}), .nCarry0(nCarry0),
    .OUT({AREG_7, StatusFlags}));
  PCRegister PC (
    .nOE(nPCSel), .IN({AREG_7, StatusFlags}), .nLDL(nPCLCLK), .nLDH(nPCHCLK), .CLKLOW(nPCClockLow),
    .CLKHIGH(nPCClockHigh), .OUTL(Addr[7:0]), .OUTH(Addr[15:8]));
  Register EAL (.nOE(not_1_out), .IN({AREG_7, StatusFlags}), .LD(nEALCLK), .OUT(Addr[7:0]));
  Register EAH (.nOE(not_1_out), .IN({AREG_7, StatusFlags}), .LD(nEAHCLK), .OUT(Addr[15:8]));
  LED u_nBITOP (.in(not_2_out));
  not not_2 (not_2_out, CtrlWord[36]);
  LED u_nShiftRight (.in(not_3_out));
  LED u_nSBC (.in(not_4_out));
  not not_3 (not_3_out, CtrlWord[34]);
  not not_4 (not_4_out, CtrlWord[35]);
  _8BitBuffer _8bitbuffer_1 (.nOE(nPCLOE), .IN(Addr[7:0]), .OUT({AREG_7, StatusFlags}));
  _8BitBuffer _8bitbuffer_2 (.nOE(nPCHOE), .IN(Addr[15:8]), .OUT({AREG_7, StatusFlags}));
  LED nFlagInstr (.in(not_5_out));
  not not_5 (not_5_out, CtrlWord[33]);
  STRegister stregister_1 (
    .nOE(nSTREGOE), .IN({AREG_7, StatusFlags}), .nLD(nSTREGCLK), .nFlagInstr(nFlagInst), .InstReg(INSTR),
    .CLK(CLK), .nShiftRight(nShiftRight), .nCarry8(nCarry8), .nBITOP(nBITOP), .nSBC(nSBC), .BREG0(BREG_0),
    .BREG6(BREG_6), .BREG7(BREG_7), .AREG7(AREG_7), .SUM7(SUM_7), .nUpdateC(nUpdateC), .nUpdateNZ(nUpdateNZ),
    .nUpdateV(nUpdateV), .nCarry(nDecimal), .nDecimal(nCarry), .OUT({AREG_7, StatusFlags}));
  LED u_NoBCD (.in(CtrlWord[32]));
  AddrDecode addrdecode_1 (
    .ADDR(Addr), .nMAccess(nMAccess), .nCSRAM0(addrdecode_1_ncsram0), .nCSRAM1(addrdecode_1_ncsram1),
    .nCSROM(addrdecode_1_ncsrom));  // open: nCSKB, nCSTERM
  LED u_nUpdateC (.in(not_6_out));
  LED u_nUpdateV (.in(not_7_out));
  not not_6 (not_6_out, CtrlWord[30]);
  not not_7 (not_7_out, CtrlWord[31]);
  LED u_nUpdateNZ (.in(not_8_out));
  not not_8 (not_8_out, CtrlWord[29]);
  LED u_CarryONE (.in(CtrlWord[28]));
  MemoryBank memorybank_1 (
    .DATA(memorybank_1_data), .ADDR(Addr), .nMWrite(nMWrite), .nCSRAM0(addrdecode_1_ncsram0),
    .nCSRAM1(addrdecode_1_ncsram1), .nCSROM(addrdecode_1_ncsrom));
  Seven_Seg_Hex seven_seg_hex_1 (.d({1'b0, CtrlWord[26:24]}), .dp(1'b0));
  LED u_CarryZERO (.in(CtrlWord[27]));
  LED u_nPCSel (.in(not_9_out));
  not not_9 (not_9_out, CtrlWord[23]);
  LED u_nMWrite (.in(not_10_out));
  not not_10 (not_10_out, CtrlWord[22]);
  // Probe on SEQCNT
  // Probe on INSTR
  // Probe on Addr
  LED ILoad (.in(CtrlWord[20]));
  LED u_nMAccess (.in(not_11_out));
  not not_11 (not_11_out, CtrlWord[21]);
  _74245_RD _74245_rd_1 (
    .nOE(nMAccess), .DIR(nMWrite), .A1(memorybank_1_data[0]), .A2(memorybank_1_data[1]),
    .A3(memorybank_1_data[2]), .A4(memorybank_1_data[3]), .A5(memorybank_1_data[4]),
    .A6(memorybank_1_data[5]), .A7(memorybank_1_data[6]), .A8(memorybank_1_data[7]), .B1(StatusFlags[0]),
    .B2(StatusFlags[1]), .B3(StatusFlags[2]), .B4(StatusFlags[3]), .B5(StatusFlags[4]), .B6(StatusFlags[5]),
    .B7(StatusFlags[6]), .B8(AREG_7), .VCC(1'b1), .GND(1'b0));
  LED u_nPCHCLK (.in(not_12_out));
  not not_12 (not_12_out, CtrlWord[19]);
  // Probe on {AREG_7, StatusFlags}
  LED u_nPCLCLK (.in(not_13_out));
  not not_13 (not_13_out, CtrlWord[18]);
  // Probe on CtrlWord[16:12]
  LED nSeqRst (.in(not_14_out));
  not not_14 (not_14_out, CtrlWord[17]);
  Seven_Seg_Hex seven_seg_hex_2 (.d(CtrlWord[7:4]), .dp(1'b0));
  Seven_Seg_Hex seven_seg_hex_3 (.d(CtrlWord[11:8]), .dp(1'b0));
  // Probe on {AREG_7, StatusFlags}
  LED N (.in(StatusFlags[0]));
  LED V (.in(StatusFlags[1]));
  LED page (.in(StatusFlags[2]));
  LED B_2 (.in(StatusFlags[3]));
  LED D (.in(StatusFlags[4]));
  LED I (.in(StatusFlags[5]));
  LED Z (.in(StatusFlags[6]));
  LED C (.in(AREG_7));
  Seven_Seg_Hex seven_seg_hex_4 (.d(CtrlWord[3:0]), .dp(1'b0));
  // Probe on CtrlWord

  // Other names for the same wires on the sheet: StatusFlags[7] = AREG_7; RSTBTN = RESET

  // Notes on the sheet:
  //   CLK: Hz: 3
  //   RESET: default 1
  //   ==>
  //   W Bus
  //   A-Bus
  //   STA (zeropage)
  //   00085: IREGLOAD | PCCLOCKLO | PCCLOCKHI | (HIZ << DRIVER) | MEMACCESS | PCSEL           BC000E
  //   00185: (EAH << LOAD) | (CONSTR << DRIVER)                                               0000BF
  //   00285: (EAL << LOAD) | (HIZ << DRIVER) | MEMACCESS | PCCLOCKLO | PCCLOCKHI | PCSEL      AC00EE
  //   00385: (AREG << DRIVER) | MEMACCESS | MWRITE | UCOUNTERRESET                            620001
  //   Mem Buffer
  //   ALUOp
  //   Constant
  //   DEST
  //   SRC
  //   24: 000CEF
  //   25: 000FBF
  //   26: 24006E
  //   27: 000DEF
  //   28: 28003E
  //   29: 020F4F
endmodule
