// Digital circuit Carry0.dig as structural Verilog
module Carry0 (
  input  nCarry,
  input  CarryZERO,
  input  CarryONE,
  output nCarry0
);

  wire and_1_out, not_1_out;

  not not_1 (not_1_out, CarryONE);
  and and_1 (and_1_out, nCarry, not_1_out);
  or or_1 (nCarry0, and_1_out, CarryZERO);
endmodule

/* Test case:
~Carry  CarryONE  CarryZERO  ~Carry0
     0         0          0        0
     0         0          1        1
     0         1          0        0

     1         0          0        1
     1         0          1        1
     1         1          0        0
*/
