// Digital circuit ConstRegister.dig as structural Verilog
module ConstRegister (
  input  [7:0] IN,
  input  nOE,
  output [7:0] OUT
);

  wire [7:0] bitextender_1_out;

  BitExtender #(.inputBits(4), .outputBits(8)) bitextender_1 (.in(IN[3:0]), .out(bitextender_1_out));
  _74245_RD _74245_rd_1 (
    .nOE(nOE), .DIR(1'b1), .A1(bitextender_1_out[0]), .A2(bitextender_1_out[1]), .A3(bitextender_1_out[2]),
    .A4(bitextender_1_out[3]), .A5(bitextender_1_out[4]), .A6(bitextender_1_out[5]),
    .A7(bitextender_1_out[6]), .A8(bitextender_1_out[7]), .B1(OUT[0]), .B2(OUT[1]), .B3(OUT[2]), .B4(OUT[3]),
    .B5(OUT[4]), .B6(OUT[5]), .B7(OUT[6]), .B8(OUT[7]), .VCC(1'b1), .GND(1'b0));
  // Pins of 4 and 8 bits meet at IN
endmodule
