// Digital circuit EARegister.dig as structural Verilog
module EARegister (
  input  CP,
  input  [7:0] IN,
  input  nOE,
  output [7:0] OUT
);

  wire _74173_rd_1_q0, _74173_rd_1_q1, _74173_rd_1_q2, _74173_rd_2_q0, _74173_rd_2_q1, _74173_rd_2_q2,
       _74173_rd_2_q3;

  _74173_RD _74173_rd_1 (
    .D0(IN[0]), .D1(IN[1]), .D2(IN[2]), .D3(IN[3]), .nE1(1'b0), .nE2(1'b0), .CP(CP), .MR(1'b0), .nOE(1'b0),
    .nOE2(1'b0), .Q0(_74173_rd_1_q0), .Q1(_74173_rd_1_q1), .Q2(_74173_rd_1_q2), .Q3(_74173_rd_1_q2),
    .VCC(1'b1), .GND(1'b0));
  _74173_RD _74173_rd_2 (
    .D0(IN[4]), .D1(IN[5]), .D2(IN[6]), .D3(IN[7]), .nE1(1'b0), .nE2(1'b0), .CP(CP), .MR(1'b0), .nOE(1'b0),
    .nOE2(1'b0), .Q0(_74173_rd_2_q0), .Q1(_74173_rd_2_q1), .Q2(_74173_rd_2_q2), .Q3(_74173_rd_2_q3),
    .VCC(1'b1), .GND(1'b0));
  _74245_RD _74245_rd_1 (
    .nOE(nOE), .DIR(1'b1), .A1(_74173_rd_1_q0), .A2(_74173_rd_1_q1), .A3(_74173_rd_1_q2),
    .A4(_74173_rd_1_q2), .A5(_74173_rd_2_q0), .A6(_74173_rd_2_q1), .A7(_74173_rd_2_q2), .A8(_74173_rd_2_q3),
    .B1(OUT[0]), .B2(OUT[1]), .B3(OUT[2]), .B4(OUT[3]), .B5(OUT[4]), .B6(OUT[5]), .B7(OUT[6]), .B8(OUT[7]),
    .VCC(1'b1), .GND(1'b0));
endmodule
