// Digital circuit EqualsZero.dig as structural Verilog
module EqualsZero (
  input  [7:0] IN,
  output OUT
);

  wire or_1_out, or_2_out, or_3_out, or_4_out, or_5_out, or_6_out;

  or or_1 (or_1_out, IN[0], IN[1]);
  or or_2 (or_2_out, IN[2], IN[3]);
  or or_3 (or_3_out, IN[4], IN[5]);
  or or_4 (or_4_out, IN[6], IN[7]);
  or or_5 (or_5_out, or_1_out, or_2_out);
  or or_6 (or_6_out, or_3_out, or_4_out);
  or or_7 (OUT, or_5_out, or_6_out);
endmodule

/* Test case:
   IN OUT
loop(i, 255)
   (i)  (ite(i=0,0,1))
end loop
*/
