// Digital circuit MemoryBank.dig as structural Verilog
module MemoryBank (
  input  nMWrite,
  input  nCSRAM0,
  input  nCSRAM1,
  input  nCSROM,
  input  [15:0] ADDR,
  output [7:0] DATA
);

  wire MWrite;

  not not_1 (MWrite, nMWrite);
  RAMSinglePortSel #(.AddrBits(14), .Bits(8)) _16K (
    .A(ADDR[13:0]), .CS(~nCSRAM0), .WE(~nMWrite), .OE(~MWrite), .D(DATA));
  RAMSinglePortSel #(.AddrBits(14), .Bits(8)) _16K_2 (
    .A(ADDR[13:0]), .CS(~nCSRAM1), .WE(~nMWrite), .OE(~MWrite), .D(DATA));
  EEPROM #(.AddrBits(14), .Bits(8)) _16K_3 (.A(ADDR[13:0]), .CS(~nCSROM), .WE(1'b0), .OE(~1'b0), .D(DATA));

  // Other names for the same wires on the sheet: ADDR14[13:0] = ADDR[13:0]

  // Notes on the sheet:
  //   nMWrite: default 1
  //   nCSRAM0: default 1
  //   nCSRAM1: default 1
  //   nCSROM: default 1
  //   ADDR: default 65532
  //   contents of _16K_3 (hex, n*v repeats v):
  //   16128*0,a9,1f,8d,3,50,a9,b,8d,2,50,a9,1b,c9,8,f0,13,c9,1b,f0,3
  //   ,c8,10,f,a9,5c,20,ef,ff,a9,d,20,ef,ff,a0,1,88,30,f6,ad,1,50,29
  //   ,8,f0,f9,ad,0,50,99,0,2,20,ef,ff,c9,d,d0,d2,a0,ff,a9,0,aa,a,a
  //   ,85,2b,c8,b9,0,2,c9,d,f0,d1,c9,2e,90,f4,f0,ee,c9,3a,f0,eb,c9,52
  //   ,f0,3b,86,28,86,29,84,2a,b9,0,2,49,30,c9,a,90,6,69,88,c9,fa,90
  //   ,11,4*a,a2,4,a,26,28,26,29,ca,d0,f8,c8,d0,e0,c4,2a,f0,94,24,2b
  //   ,50,10,a5,28,81,26,e6,26,d0,b5,e6,27,4c,44,ff,6c,24,0,30,2b,a2
  //   ,2,b5,27,95,25,95,23,ca,d0,f7,d0,14,a9,d,20,ef,ff,a5,25,20,dc
  //   ,ff,a5,24,20,dc,ff,a9,3a,20,ef,ff,a9,20,20,ef,ff,a1,24,20,dc,ff
  //   ,86,2b,a5,24,c5,28,a5,25,e5,29,b0,c1,e6,24,d0,2,e6,25,a5,24,29
  //   ,7,10,c8,48,4*4a,20,e5,ff,68,29,f,9,30,c9,3a,90,2,69,6,48,8d,0
  //   ,50,a9,ff,3a,d0,fd,68,60,0,f,0,ff
endmodule
