// Digital circuit PCRegister.dig as structural Verilog
module PCRegister (
  input  nOE,
  input  [7:0] IN,
  input  nLDL,
  input  nLDH,
  input  CLKLOW,
  input  CLKHIGH,
  output [7:0] OUTL,
  output [7:0] OUTH
);

  wire _74161_rd_1_q0, _74161_rd_1_q1, _74161_rd_1_q2, _74161_rd_1_q3, _74161_rd_1_tc, _74161_rd_2_q0,
       _74161_rd_2_q1, _74161_rd_2_q2, _74161_rd_2_q3, _74161_rd_2_tc, _74161_rd_3_q0, _74161_rd_3_q1,
       _74161_rd_3_q2, _74161_rd_3_q3, _74161_rd_3_tc, _74161_rd_4_q0, _74161_rd_4_q1, _74161_rd_4_q2,
       _74161_rd_4_q3;

  _74161_RD _74161_rd_1 (
    .A(IN[0]), .B(IN[1]), .C(IN[2]), .D(IN[3]), .nSPE(nLDL), .CP(CLKLOW), .nMR(1'b1), .PE(1'b1), .TE(1'b1),
    .Q0(_74161_rd_1_q0), .Q1(_74161_rd_1_q1), .Q2(_74161_rd_1_q2), .Q3(_74161_rd_1_q3), .TC(_74161_rd_1_tc),
    .VCC(1'b1), .GND(1'b0));
  _74161_RD _74161_rd_2 (
    .A(IN[4]), .B(IN[5]), .C(IN[6]), .D(IN[7]), .nSPE(nLDL), .CP(CLKLOW), .nMR(1'b1), .PE(1'b1),
    .TE(_74161_rd_1_tc), .Q0(_74161_rd_2_q0), .Q1(_74161_rd_2_q1), .Q2(_74161_rd_2_q2), .Q3(_74161_rd_2_q3),
    .TC(_74161_rd_2_tc), .VCC(1'b1), .GND(1'b0));
  _74161_RD _74161_rd_3 (
    .A(IN[0]), .B(IN[1]), .C(IN[2]), .D(IN[3]), .nSPE(nLDH), .CP(CLKHIGH), .nMR(1'b1), .PE(1'b1),
    .TE(_74161_rd_2_tc), .Q0(_74161_rd_3_q0), .Q1(_74161_rd_3_q1), .Q2(_74161_rd_3_q2), .Q3(_74161_rd_3_q3),
    .TC(_74161_rd_3_tc), .VCC(1'b1), .GND(1'b0));
  _74161_RD _74161_rd_4 (
    .A(IN[4]), .B(IN[5]), .C(IN[6]), .D(IN[7]), .nSPE(nLDH), .CP(CLKHIGH), .nMR(1'b1), .PE(1'b1),
    .TE(_74161_rd_3_tc), .Q0(_74161_rd_4_q0), .Q1(_74161_rd_4_q1), .Q2(_74161_rd_4_q2), .Q3(_74161_rd_4_q3),
    .VCC(1'b1), .GND(1'b0));  // open: TC
  _74245_RD _74245_rd_1 (
    .nOE(nOE), .DIR(1'b1), .A1(_74161_rd_1_q0), .A2(_74161_rd_1_q1), .A3(_74161_rd_1_q2),
    .A4(_74161_rd_1_q3), .A5(_74161_rd_2_q0), .A6(_74161_rd_2_q1), .A7(_74161_rd_2_q2), .A8(_74161_rd_2_q3),
    .B1(OUTL[0]), .B2(OUTL[1]), .B3(OUTL[2]), .B4(OUTL[3]), .B5(OUTL[4]), .B6(OUTL[5]), .B7(OUTL[6]),
    .B8(OUTL[7]), .VCC(1'b1), .GND(1'b0));
  _74245_RD _74245_rd_2 (
    .nOE(nOE), .DIR(1'b1), .A1(_74161_rd_3_q0), .A2(_74161_rd_3_q1), .A3(_74161_rd_3_q2),
    .A4(_74161_rd_3_q3), .A5(_74161_rd_4_q0), .A6(_74161_rd_4_q1), .A7(_74161_rd_4_q2), .A8(_74161_rd_4_q3),
    .B1(OUTH[0]), .B2(OUTH[1]), .B3(OUTH[2]), .B4(OUTH[3]), .B5(OUTH[4]), .B6(OUTH[5]), .B7(OUTH[6]),
    .B8(OUTH[7]), .VCC(1'b1), .GND(1'b0));

  // Other names for the same wires on the sheet: INLNIB[3:0] = IN[3:0]; INHNIB[3:0] = IN[7:4]; LDH = nLDH; LDL = nLDL

  // Notes on the sheet:
  //   nOE: default 1
  //   nLDL: default 1
  //   nLDH: default 1
endmodule

/* Test case Increment:
   ~OE   IN ~LDL ~LDH CLKLOW CLKHIGH  OUTL        OUTH
loop(i, 512)
     0 0x00    1    1      0       0   (i)           x
     0 0x00    1    1      1       1 (i+1) ((i+1)/256)
 end loop
*/

/* Test case LoadLow:
   ~OE   IN  ~LDL ~LDH CLKLOW CLKHIGH OUTL OUTH
     0 0xA5     0    1      0       0    0    x
     0 0xA5     0    1      1       0 0xA5    x
*/

/* Test case LoadHigh:
   ~OE   IN ~LDL ~LDH CLKLOW CLKHIGH OUTL OUTH
     0 0xCD    1    0      0       0    x    0
     0 0xCD    1    0      0       1    x 0xCD
*/
