// Digital circuit PageFlag.dig as structural Verilog
module PageFlag (
  input  nCARRY8,
  input  nALUOE,
  output Page
);

  wire nand_1_out, nand_2_out, nand_3_out;

  nand nand_1 (nand_1_out, nCARRY8, nALUOE);
  nand nand_2 (nand_2_out, nand_1_out, nALUOE);
  nand nand_3 (nand_3_out, nand_1_out, Page);
  nand nand_4 (Page, nand_3_out, nand_2_out);
endmodule

/* Test case:
~CARRY8  ~ALUOE  Page
# transparent
0        1      1
1        1      0
# latch last
0        1      1
1        0      1
# latch last
1        1      0
1        0      0
*/
