// Digital circuit PowerOnReset.dig as structural Verilog
module PowerOnReset (
  input  MSTRRST,
  input  CLK,
  output RESET,
  output nRESET
);

  wire _74161_rd_1_tc, nRST, POR_out;
  wire [3:0] _74161_rd_1_q0;

  Reset #(.invertOutput("false")) POR (.out(POR_out));
  nor nor_1 (nRST, MSTRRST, POR_out);
  Break break_1 (.brk(POR_out));
  _74161_RD _74161_rd_1 (
    .A(1'b0), .B(1'b0), .C(1'b0), .D(1'b0), .nSPE(1'b1), .CP(CLK), .nMR(nRST), .PE(1'b1), .TE(1'b1),
    .Q0(_74161_rd_1_q0[0]), .Q1(_74161_rd_1_q0[1]), .Q2(_74161_rd_1_q0[2]), .Q3(_74161_rd_1_q0[3]),
    .TC(_74161_rd_1_tc), .VCC(1'b1), .GND(1'b0));
  // Probe Count on _74161_rd_1_q0
  RS_FF_AS rs_ff_as_1 (.S(MSTRRST), .R(_74161_rd_1_tc), .Q(RESET), .nQ(nRESET));

  // Other names for the same wires on the sheet: RST = MSTRRST

  // Notes on the sheet:
  //   CLK: Hz: 8
endmodule
