// Digital circuit Register.dig as structural Verilog
module Register (
  input  [7:0] IN,
  input  LD,
  input  nOE,
  output [7:0] OUT
);

  _74574_RD _74574_rd_1 (
    .Q0(OUT[0]), .Q1(OUT[1]), .Q2(OUT[2]), .Q3(OUT[3]), .Q4(OUT[4]), .Q5(OUT[5]), .Q6(OUT[6]), .Q7(OUT[7]),
    .nOE(nOE), .D0(IN[0]), .D1(IN[1]), .D2(IN[2]), .D3(IN[3]), .D4(IN[4]), .D5(IN[5]), .D6(IN[6]),
    .D7(IN[7]), .CLK(LD), .VCC(1'b1), .GND(1'b0));
endmodule
