// Digital circuit RightShifter.dig as structural Verilog
module RightShifter (
  input  nCarry0,
  input  nShiftRight,
  input  [7:0] BREG,
  output [7:0] OUT
);

  _74245_RD _74245_rd_1 (
    .nOE(nShiftRight), .DIR(1'b1), .A1(BREG[1]), .A2(BREG[2]), .A3(BREG[3]), .A4(BREG[4]), .A5(BREG[5]),
    .A6(BREG[6]), .A7(BREG[7]), .A8(nCarry0), .B1(OUT[0]), .B2(OUT[1]), .B3(OUT[2]), .B4(OUT[3]),
    .B5(OUT[4]), .B6(OUT[5]), .B7(OUT[6]), .B8(OUT[7]), .VCC(1'b1), .GND(1'b0));
endmodule

/* Test case:
~ShiftRight BREG ~Carry0 OUT
 0           2    0      1
 0           2    1      (-127)
*/
