// Digital circuit SeqCounter.dig as structural Verilog
module SeqCounter (
  input  RESET,
  input  nSEQRST,
  input  CLK,
  output [4:0] COUNT
);

  wire _74161_rd_1_tc, nRESET;

  not not_1 (nRESET, RESET);
  _74161_RD _74161_rd_1 (
    .A(1'b0), .B(1'b0), .C(1'b0), .D(RESET), .nSPE(nRESET), .CP(CLK), .nMR(nSEQRST), .PE(1'b1), .TE(1'b1),
    .Q0(COUNT[0]), .Q1(COUNT[1]), .Q2(COUNT[2]), .Q3(COUNT[3]), .TC(_74161_rd_1_tc), .VCC(1'b1), .GND(1'b0));
  _74161_RD _74161_rd_2 (
    .A(RESET), .B(1'b0), .C(1'b0), .D(1'b0), .nSPE(nRESET), .CP(CLK), .nMR(nSEQRST), .PE(1'b1),
    .TE(_74161_rd_1_tc), .Q0(COUNT[4]), .VCC(1'b1), .GND(1'b0));  // open: Q1, Q2, Q3, TC

  // Notes on the sheet:
  //   nSEQRST: default 1
  //   CLK: Hz: 3
endmodule

/* Test case CountUp:
   CLK RESET ~SEQRST COUNT
   0   0        1      0
loop(i, 31)
   c   0        1      (i+1)
end loop

   c   0        1      0
*/

/* Test case ~SEQRST:
   CLK RESET ~SEQRST COUNT
   0   0        1      0
   c   0        1      1
   c   0        1      2
   c   0        1      3
   c   0        0      0
   c   0        1      1
*/

/* Test case MSTRRST:
   CLK RESET ~SEQRST COUNT
   0   0        1      0
   c   0        1      1
   c   0        1      2
   c   1        1      24
   c   0        1      25
*/
