// Digital circuit Sequencer.dig as structural Verilog
module Sequencer (
  input  CLK,
  input  [7:0] INSTR,
  input  [7:0] Status,
  input  MSTRRST,
  input  nCarry8,
  input  BREG_7,
  output nALUOE,
  output nAREGOE,
  output nAREGCLK,
  output nBREGOE,
  output nBREGCLK,
  output nPCHOE,
  output nPCHCLK,
  output nSPREGOE,
  output nSPREGCLK,
  output nEBHOE,
  output nEBHCLK,
  output nPCLOE,
  output nPCLCLK,
  output nACCOE,
  output nACCCLK,
  output nEBLOE,
  output nEBLCLK,
  output nSTREGOE,
  output nSTREGCLK,
  output nEAHOE,
  output nEAHCLK,
  output nXREGOE,
  output nXREGCLK,
  output nYREGOE,
  output nYREGCLK,
  output nEALOE,
  output nEALCLK,
  output nCONSTOE,
  output [3:0] Constant,
  output [4:0] ALUOp,
  output nPCClockLow,
  output nPCClockHigh,
  output IREGLoad,
  output nMemAccess,
  output nMWrite,
  output nPCSel,
  output CarryZERO,
  output CarryONE,
  output nUpdateNZ,
  output nUpdateC,
  output nUpdateV,
  output NoBCD,
  output nFlagInst,
  output nShiftRight,
  output nSBC,
  output nBITOP,
  output [39:0] CtrlWord,
  output [4:0] COUNT
);

  wire _74138_rd_1_ny0, _74138_rd_1_ny1, _74138_rd_1_ny2, _74138_rd_1_ny3, _74138_rd_1_ny4, _74138_rd_1_ny5,
       _74138_rd_1_ny6, _74138_rd_1_ny7, _74138_rd_2_ny0, _74138_rd_2_ny1, _74138_rd_2_ny2, _74138_rd_2_ny3,
       _74138_rd_2_ny4, _74138_rd_2_ny5, _74138_rd_2_ny6, _74138_rd_2_ny7, _74138_rd_3_ny0, _74138_rd_3_ny1,
       _74138_rd_3_ny2, _74138_rd_3_ny3, _74138_rd_3_ny4, _74138_rd_3_ny5, _74138_rd_3_ny6, _74138_rd_3_ny7,
       _74138_rd_4_ny0, _74138_rd_4_ny1, _74138_rd_4_ny2, _74138_rd_4_ny3, _74138_rd_4_ny4, _74138_rd_4_ny5,
       _74138_rd_4_ny6, _74138_rd_4_ny7, _74574_rd_2_q1, _74574_rd_3_q0, _74574_rd_4_q1, _74574_rd_4_q7,
       _74574_rd_8_q5, _74574_rd_8_q6, _74574_rd_8_q7, CLKLATCH, FLAG0, FLAG1, FLAG2, nSEQRST, Page;
  wire [13:13] _74151_rd_1_y;

  PageFlag pageflag_1 (.nCARRY8(nCarry8), .nALUOE(nALUOE), .Page(Page));
  not not_1 (CLKLATCH, CLK);
  SeqCounter seqcounter_1 (.CLK(CLK), .RESET(MSTRRST), .nSEQRST(nSEQRST), .COUNT(COUNT));
  _74151_RD _74151_rd_1 (
    .Y(_74151_rd_1_y[13]), .nG(1'b0), .D0(Status[0]), .D1(Status[1]), .D2(Status[2]), .D3(Status[3]),
    .D4(BREG_7), .D5(Page), .D6(Status[6]), .D7(Status[7]), .A(FLAG0), .B(FLAG1), .C(FLAG2), .VCC(1'b1),
    .GND(1'b0));  // open: W
  // Probe Address on {_74151_rd_1_y[13], COUNT, INSTR}
  MicrocodeROM microcoderom_1 (.ADDR({_74151_rd_1_y[13], COUNT, INSTR}), .nCS(1'b0), .nOE(1'b0), .DATA(CtrlWord));
  _74138_RD _74138_rd_1 (
    .A0(CtrlWord[0]), .A1(CtrlWord[1]), .A2(CtrlWord[2]), .G(1'b1), .nGB(CtrlWord[3]), .nGA(1'b0),
    .nY0(_74138_rd_1_ny0), .nY1(_74138_rd_1_ny1), .nY2(_74138_rd_1_ny2), .nY3(_74138_rd_1_ny3),
    .nY4(_74138_rd_1_ny4), .nY5(_74138_rd_1_ny5), .nY6(_74138_rd_1_ny6), .nY7(_74138_rd_1_ny7), .VCC(1'b1),
    .GND(1'b0));
  _74138_RD _74138_rd_2 (
    .A0(CtrlWord[0]), .A1(CtrlWord[1]), .A2(CtrlWord[2]), .G(CtrlWord[3]), .nGB(1'b0), .nGA(1'b0),
    .nY0(_74138_rd_2_ny0), .nY1(_74138_rd_2_ny1), .nY2(_74138_rd_2_ny2), .nY3(_74138_rd_2_ny3),
    .nY4(_74138_rd_2_ny4), .nY5(_74138_rd_2_ny5), .nY6(_74138_rd_2_ny6), .nY7(_74138_rd_2_ny7), .VCC(1'b1),
    .GND(1'b0));
  _74138_RD _74138_rd_3 (
    .A0(CtrlWord[4]), .A1(CtrlWord[5]), .A2(CtrlWord[6]), .G(1'b1), .nGB(CtrlWord[7]), .nGA(1'b0),
    .nY0(_74138_rd_3_ny0), .nY1(_74138_rd_3_ny1), .nY2(_74138_rd_3_ny2), .nY3(_74138_rd_3_ny3),
    .nY4(_74138_rd_3_ny4), .nY5(_74138_rd_3_ny5), .nY6(_74138_rd_3_ny6), .nY7(_74138_rd_3_ny7), .VCC(1'b1),
    .GND(1'b0));
  _74138_RD _74138_rd_4 (
    .A0(CtrlWord[4]), .A1(CtrlWord[5]), .A2(CtrlWord[6]), .G(CtrlWord[7]), .nGB(1'b0), .nGA(1'b0),
    .nY0(_74138_rd_4_ny0), .nY1(_74138_rd_4_ny1), .nY2(_74138_rd_4_ny2), .nY3(_74138_rd_4_ny3),
    .nY4(_74138_rd_4_ny4), .nY5(_74138_rd_4_ny5), .nY6(_74138_rd_4_ny6), .nY7(_74138_rd_4_ny7), .VCC(1'b1),
    .GND(1'b0));
  _74574_RD _74574_rd_1 (
    .Q0(nALUOE), .Q1(nAREGOE), .Q2(nBREGOE), .Q3(nPCHOE), .Q4(nSPREGOE), .Q5(nEBHOE), .Q6(nPCLOE),
    .Q7(nACCOE), .nOE(1'b0), .D0(_74138_rd_1_ny0), .D1(_74138_rd_1_ny1), .D2(_74138_rd_1_ny2),
    .D3(_74138_rd_1_ny3), .D4(_74138_rd_1_ny4), .D5(_74138_rd_1_ny5), .D6(_74138_rd_1_ny6),
    .D7(_74138_rd_1_ny7), .CLK(CLKLATCH), .VCC(1'b1), .GND(1'b0));
  _74574_RD _74574_rd_2 (
    .Q0(nEBLOE), .Q1(_74574_rd_2_q1), .Q2(nSTREGOE), .Q3(nEAHOE), .Q4(nXREGOE), .Q5(nYREGOE), .Q6(nEALOE),
    .Q7(nCONSTOE), .nOE(1'b0), .D0(_74138_rd_2_ny0), .D1(_74138_rd_2_ny1), .D2(_74138_rd_2_ny2),
    .D3(_74138_rd_2_ny3), .D4(_74138_rd_2_ny4), .D5(_74138_rd_2_ny5), .D6(_74138_rd_2_ny6),
    .D7(_74138_rd_2_ny7), .CLK(CLKLATCH), .VCC(1'b1), .GND(1'b0));
  _74574_RD _74574_rd_3 (
    .Q0(_74574_rd_3_q0), .Q1(nAREGCLK), .Q2(nBREGCLK), .Q3(nPCHCLK), .Q4(nSPREGCLK), .Q5(nEBHCLK),
    .Q6(nPCLCLK), .Q7(nACCCLK), .nOE(1'b0), .D0(_74138_rd_3_ny0), .D1(_74138_rd_3_ny1), .D2(_74138_rd_3_ny2),
    .D3(_74138_rd_3_ny3), .D4(_74138_rd_3_ny4), .D5(_74138_rd_3_ny5), .D6(_74138_rd_3_ny6),
    .D7(_74138_rd_3_ny7), .CLK(CLKLATCH), .VCC(1'b1), .GND(1'b0));
  _74574_RD _74574_rd_4 (
    .Q0(nEBLCLK), .Q1(_74574_rd_4_q1), .Q2(nSTREGCLK), .Q3(nEAHCLK), .Q4(nXREGCLK), .Q5(nYREGCLK),
    .Q6(nEALCLK), .Q7(_74574_rd_4_q7), .nOE(1'b0), .D0(_74138_rd_4_ny0), .D1(_74138_rd_4_ny1),
    .D2(_74138_rd_4_ny2), .D3(_74138_rd_4_ny3), .D4(_74138_rd_4_ny4), .D5(_74138_rd_4_ny5),
    .D6(_74138_rd_4_ny6), .D7(_74138_rd_4_ny7), .CLK(CLKLATCH), .VCC(1'b1), .GND(1'b0));
  _74574_RD _74574_rd_5 (
    .Q0(Constant[0]), .Q1(Constant[1]), .Q2(Constant[2]), .Q3(Constant[3]), .Q4(ALUOp[0]), .Q5(ALUOp[1]),
    .Q6(ALUOp[2]), .Q7(ALUOp[3]), .nOE(1'b0), .D0(CtrlWord[8]), .D1(CtrlWord[9]), .D2(CtrlWord[10]),
    .D3(CtrlWord[11]), .D4(CtrlWord[12]), .D5(CtrlWord[13]), .D6(CtrlWord[14]), .D7(CtrlWord[15]),
    .CLK(CLKLATCH), .VCC(1'b1), .GND(1'b0));
  _74574_RD _74574_rd_6 (
    .Q0(ALUOp[4]), .Q1(nSEQRST), .Q2(nPCClockLow), .Q3(nPCClockHigh), .Q4(IREGLoad), .Q5(nMemAccess),
    .Q6(nMWrite), .Q7(nPCSel), .nOE(1'b0), .D0(CtrlWord[16]), .D1(CtrlWord[17]), .D2(CtrlWord[18]),
    .D3(CtrlWord[19]), .D4(CtrlWord[20]), .D5(CtrlWord[21]), .D6(CtrlWord[22]), .D7(CtrlWord[23]),
    .CLK(CLKLATCH), .VCC(1'b1), .GND(1'b0));
  _74574_RD _74574_rd_7 (
    .Q0(FLAG0), .Q1(FLAG1), .Q2(FLAG2), .Q3(CarryZERO), .Q4(CarryONE), .Q5(nUpdateNZ), .Q6(nUpdateC),
    .Q7(nUpdateV), .nOE(1'b0), .D0(CtrlWord[24]), .D1(CtrlWord[25]), .D2(CtrlWord[26]), .D3(CtrlWord[27]),
    .D4(CtrlWord[28]), .D5(CtrlWord[29]), .D6(CtrlWord[30]), .D7(CtrlWord[31]), .CLK(CLKLATCH), .VCC(1'b1),
    .GND(1'b0));
  _74574_RD _74574_rd_8 (
    .Q0(NoBCD), .Q1(nFlagInst), .Q2(nShiftRight), .Q3(nSBC), .Q4(nBITOP), .Q5(_74574_rd_8_q5),
    .Q6(_74574_rd_8_q6), .Q7(_74574_rd_8_q7), .nOE(1'b0), .D0(CtrlWord[32]), .D1(CtrlWord[33]),
    .D2(CtrlWord[34]), .D3(CtrlWord[35]), .D4(CtrlWord[36]), .D5(CtrlWord[37]), .D6(CtrlWord[38]),
    .D7(CtrlWord[39]), .CLK(CLKLATCH), .VCC(1'b1), .GND(1'b0));

  // Other names for the same wires on the sheet: BREG7 = BREG_7

  // Notes on the sheet:
  //   INSTR: default 133
  //   Reset
  //   --------
  //   24: 000CEF
  //   25: 000FBF
  //   26: 24006E
  //   27: 000DEF
  //   28: 28003E
  //   29: 020F4F
  //   0-3
  //   4-7
  //   8-15
  //   16-23
  //   24-31
  //   32-39
endmodule

/* Test case Reset:
  CLK MSTRRST INSTR Status BREG_7 ~Carry8 ~EAHCLK ~EALCLK ~PCHCLK ~PCLCLK ~SPREGCLK ~CONSTOE Constant COUNT CtrlWord
# 24: (EAL << LOAD) | (CONSTR << DRIVER) | (0x0c << CONSTANT)
    c       1  0xEA      0      x      x        1       0       1       1         1        0     0x0C    24        x

# 25: (EAH << LOAD) | (CONSTR << DRIVER) | (0x0f << CONSTANT) 
# CLK MSTRRST INSTR Status BREG_7 ~Carry8 ~EAHCLK ~EALCLK ~PCHCLK ~PCLCLK ~SPREGCLK ~CONSTOE Constant COUNT CtrlWord
    c       0  0x85      0      0      0        0       1       1       1         1        0     0x0F    25        x

# 26: (PCL << LOAD) | (HIZ << DRIVER) | MEMACCESS | PCCLOCKLO 
# CLK MSTRRST INSTR Status BREG_7 ~Carry8 ~EAHCLK ~EALCLK ~PCHCLK ~PCLCLK ~SPREGCLK ~CONSTOE Constant COUNT CtrlWord
    c       0  0x85      0      0      0        1       1       1       0         1        1        x    26        x

# 27: (EAL << LOAD) | (CONSTR << DRIVER) | (0x0d << CONSTANT)
# CLK MSTRRST INSTR Status BREG_7 ~Carry8 ~EAHCLK ~EALCLK ~PCHCLK ~PCLCLK ~SPREGCLK ~CONSTOE Constant COUNT CtrlWord
    c       0  0x85      0      0      0        1       0       1       1         1        0     0x0D    27        x

# 28: (PCH << LOAD) | (HIZ << DRIVER) | MEMACCESS | PCCLOCKHI
# CLK MSTRRST INSTR Status BREG_7 ~Carry8 ~EAHCLK ~EALCLK ~PCHCLK ~PCLCLK ~SPREGCLK ~CONSTOE Constant COUNT CtrlWord
    c       0  0x85      0      0      0        1       1       0       1         1        1        x    28        x

# 29: (SPREG << LOAD) | (CONSTR << DRIVER) | (0x0f << CONSTANT) | UCOUNTERRESET
# CLK MSTRRST INSTR Status BREG_7 ~Carry8 ~EAHCLK ~EALCLK ~PCHCLK ~PCLCLK ~SPREGCLK ~CONSTOE Constant COUNT CtrlWord
    c       0  0x85      0      0      0        1       1       1       1         0        0     0x0F    29        x
*/
