// Digital circuit Top.dig as structural Verilog
module Top (
  input  CLK
);

  wire BITOP, CarryZERO, Constant, CtrlWord, FlagInst, IREGLoad, nACCCLK, nACCOE, nALUOE, nAREGCLK, nAREGOE,
       nBREGCLK, nBREGOE, nCarry8, nCONSTOE, nEAHCLK, nEAHOE, nEALCLK, nEBHCLK, nEBHOE, nEBLCLK, nEBLOE,
       nMemAccess, nMWrite, not_1_out, nPCClockHigh, nPCClockLow, nPCHCLK, nPCHOE, nPCLCLK, nPCLOE, nPCSel,
       nSPREGCLK, nSPREGOE, nSTREGOE, nUpdateC, nUpdateNZ, nUpdateV, nXREGCLK, nXREGOE, nYREGCLK, nYREGOE,
       RESET, RESET_out, SBC, ShiftRight, STREGCLK;
  wire [4:0] ALUOp;
  wire [7:0] A_out, B_out, EBH_out, INSTR, memorybank_1_data, PC_outh, PC_outl, StatusFlags;

  // Sequencer sequencer_1: pin names not known; wires that end beside it: CLK, 8'h85, {8{1'b0}}, RESET, nALUOE, nAREGOE, nAREGCLK, nBREGOE, nBREGCLK, nPCHOE, nPCHCLK, nSPREGOE, nSPREGCLK, nEBHOE, nEBHCLK, nPCLOE, nPCLCLK, nACCOE, nACCCLK, nEBLOE, nEBLCLK, nSTREGOE, STREGCLK, nEAHOE, nEAHCLK
  Register EBH (.nOE(nEBHOE), .IN(EBH_out), .LD(nEBHCLK), .OUT(EBH_out));
  Register EBL (.nOE(nEBLOE), .IN(EBH_out), .LD(nEBLCLK), .OUT(EBH_out));
  Register SP (.nOE(nSPREGOE), .IN(EBH_out), .LD(nSPREGCLK), .OUT(EBH_out));
  Register Y (.nOE(nYREGOE), .IN(EBH_out), .LD(nYREGCLK), .OUT(EBH_out));
  Register X (.nOE(nXREGOE), .IN(EBH_out), .LD(nXREGCLK), .OUT(EBH_out));
  Register ACC (.nOE(nACCOE), .IN(EBH_out), .LD(nACCCLK), .OUT(EBH_out));
  Register A (.nOE(nAREGOE), .IN(EBH_out), .LD(nAREGCLK), .OUT(A_out));
  Register B (.nOE(nBREGOE), .IN(EBH_out), .LD(nBREGCLK), .OUT(B_out));
  INSTRegister instregister_1 (.nOE(1'b0), .IN(EBH_out), .Load(IREGLoad), .OUT(INSTR));
  ALU alu_1 (.nOE(nALUOE), .A(A_out), .B(B_out), .OP(ALUOp), .nCarry8(nCarry8));  // open: OUT
  RightShifter rightshifter_1 (.nShiftRight(ShiftRight), .BREG(B_out), .nCarry0(CarryZERO));  // open: OUT
  not not_1 (not_1_out, nPCSel);
  PCRegister PC (
    .nOE(nPCSel), .IN(EBH_out), .nLDL(nPCLCLK), .nLDH(nPCHCLK), .CLKLOW(nPCClockLow), .CLKHIGH(nPCClockHigh),
    .OUTL(PC_outl), .OUTH(PC_outh));
  Register EAL (.nOE(not_1_out), .IN(EBH_out), .LD(nEALCLK), .OUT(PC_outl));
  Register EAH (.nOE(not_1_out), .IN(EBH_out), .LD(nEAHCLK), .OUT(PC_outh));
  // ConstRegister constregister_1: pin names not known; wires that end beside it: nCONSTOE, Constant, EBH_out
  _8BitBuffer _8bitbuffer_1 (.nOE(nPCLOE), .IN(PC_outl), .OUT(EBH_out));
  _8BitBuffer _8bitbuffer_2 (.nOE(nPCHOE), .IN(PC_outh), .OUT(EBH_out));
  STRegister ST (
    .CP(STREGCLK), .IN(EBH_out), .WBUS(EBH_out), .nUpdateNZ(nUpdateNZ), .BREG7(1'b0), .BREG6(1'b0),
    .nBITOP(BITOP), .nUPDATEV(nUpdateV), .nSBC(SBC), .AREG7(1'b0), .SUM7(1'b0), .InstReg(INSTR), .CLK(CLK),
    .nFlagInstr(FlagInst), .nUPDATEC(nUpdateC), .BREG0(1'b0), .nCarry8(nCarry8), .nShiftRight(ShiftRight),
    .OUT(StatusFlags));
  // Probe on {PC_outh, PC_outl}
  MemoryBank memorybank_1 (
    .ADDR({PC_outh, PC_outl}), .nMWrite(nMWrite), .nMemAccess(nMemAccess), .DATA(memorybank_1_data));
  Button u_RESET (.out(RESET_out));
  // Probe on CtrlWord
  // Probe on StatusFlags
  // Probe on INSTR
  PowerOnReset poweronreset_1 (.MSTRRST(RESET_out), .CLK(CLK), .RESET(RESET));  // open: nRESET
  _74245_RD _74245_rd_1 (
    .nOE(nMemAccess), .DIR(nMWrite), .A1(memorybank_1_data[0]), .A2(memorybank_1_data[1]),
    .A3(memorybank_1_data[2]), .A4(memorybank_1_data[3]), .A5(memorybank_1_data[4]),
    .A6(memorybank_1_data[5]), .A7(memorybank_1_data[6]), .A8(memorybank_1_data[7]), .B1(EBH_out[0]),
    .B2(EBH_out[1]), .B3(EBH_out[2]), .B4(EBH_out[3]), .B5(EBH_out[4]), .B6(EBH_out[5]), .B7(EBH_out[6]),
    .B8(EBH_out[7]), .VCC(1'b1), .GND(1'b0));

  // Notes on the sheet:
  //   CLK: Hz: 3
  //   ==>
  //   W Bus
  //   Addressing
  //   A-Bus
  //   BC000E
  //   0000BF
  //   AC00EE
  //   620001
  //   Mem Buffer
endmodule
